// Digital circuit COMPUTER.dig as structural Verilog
module COMPUTER (
  input  CLK
);

  wire ctrl_unit_1_rwe;
  wire [2:0] ctrl_unit_1_rda, ctrl_unit_1_rsa1, ctrl_unit_1_rsa2;
  wire [7:0] _8_register_bank_1_rd1, _8_register_bank_1_rd2, alu_8_1_s, PC_q;
  wire [15:0] _256_instr_mem_1_p2;

  REGISTER_8 PC (.CLK(CLK), .Q(PC_q));  // open: D, E
  // _256_INSTR_MEM _256_instr_mem_1: pin names not known; wires that end beside it: PC_q, _256_instr_mem_1_p2
  CTRL_UNIT ctrl_unit_1 (
    .INSTR(_256_instr_mem_1_p2), .RSA1(ctrl_unit_1_rsa1), .RSA2(ctrl_unit_1_rsa2), .RDA(ctrl_unit_1_rda),
    .RWE(ctrl_unit_1_rwe));  // open: RS2Im, ALOP
  _8_REGISTER_BANK _8_register_bank_1 (
    .A1(ctrl_unit_1_rsa1), .A2(ctrl_unit_1_rsa2), .A3(ctrl_unit_1_rda), .WD3(alu_8_1_s),
    .WE3(ctrl_unit_1_rwe), .CLK(CLK), .RD1(_8_register_bank_1_rd1), .RD2(_8_register_bank_1_rd2));
  ALU_8 alu_8_1 (.A(_8_register_bank_1_rd1), .B(_8_register_bank_1_rd2), .S(alu_8_1_s));  // open: OP
  _256B_MEM _256b_mem_1 ();  // open: A, WD, WE, CLK, RD
endmodule
