// Digital circuit 256_INSTR_MEM.dig as structural Verilog
module _256_INSTR_MEM (
  input  [7:0] A,
  input  [15:0] WD,
  input  WE,
  input  CLK,
  output [15:0] RD
);

  _256B_MEM _256b_mem_1 (.A(A), .WD(WD[7:0]), .WE(WE), .CLK(CLK), .RD(RD[7:0]));
  _256B_MEM _256b_mem_2 (.A(A), .WD(WD[15:8]), .WE(WE), .CLK(CLK), .RD(RD[15:8]));
endmodule
