// Digital circuit CMPU_CTRL.dig as structural Verilog
module CMPU_CTRL (
  input  [1:0] OP,
  input  Z,
  input  C,
  output Q
);

  wire not_1_out, not_2_out, or_1_out;

  not not_1 (not_1_out, Z);
  not not_2 (not_2_out, C);
  or or_1 (or_1_out, C, Z);
  Multiplexer #(.Selector_Bits(2)) multiplexer_1 (
    .sel(OP), .in_0(Z), .in_1(not_1_out), .in_2(not_2_out), .in_3(or_1_out), .out(Q));

  // Notes on the sheet:
  //   EQ
  //   NEQ
  //   LT
  //   GE
endmodule
