// Digital circuit COMPUTER.dig as structural Verilog
module COMPUTER (
  input  CLK,
  input  [15:0] ID,
  input  [7:0] DA,
  input  [1:0] MODE,
  input  [7:0] IA,
  input  [7:0] DD,
  input  [15:0] IN,
  output [7:0] out_2,
  output [7:0] out_3,
  output [7:0] out_4,
  output [47:0] OUT
);

  wire _8_register_bank_1_p6, alu_8_1_p5, alu_8_1_p6, and_1_out, and_2_out, and_4_out, cmpu_ctrl_1_p4,
       ctrl_unit_1_p2, ctrl_unit_1_p3, ctrl_unit_1_p4, ctrl_unit_1_p5, ctrl_unit_1_p6, ctrl_unit_1_p7,
       ctrl_unit_1_p8, ctrl_unit_1_p11, demultiplexer_1_out_0, demultiplexer_1_out_1, demultiplexer_1_out_2,
       demultiplexer_1_out_3, multiplexer_7_out, or_1_out, or_2_out;
  wire [1:0] ctrl_unit_1_p10, ctrl_unit_1_p12;
  wire [7:0] _8_register_bank_1_p4, _256b_mem_io_1_rd, alu_8_1_p4, ctrl_unit_1_p9, multiplexer_1_out,
       multiplexer_2_out, multiplexer_3_out, multiplexer_4_out, multiplexer_5_out, multiplexer_6_out,
       multiplexer_9_out, PC_plus_1_s, PC_plus_Imm_s;
  wire [15:0] _256_instr_mem_1_rd;

  Demultiplexer #(.Selector_Bits(2)) demultiplexer_1 (
    .sel(MODE), .in(1'b1), .out_0(demultiplexer_1_out_0), .out_1(demultiplexer_1_out_1),
    .out_2(demultiplexer_1_out_2), .out_3(demultiplexer_1_out_3));
  Multiplexer #(.Selector_Bits(2), .Bits(8)) multiplexer_1 (
    .sel(ctrl_unit_1_p12), .in_0(PC_plus_1_s), .in_1(ctrl_unit_1_p9), .in_2(out_2), .in_3(multiplexer_9_out),
    .out(multiplexer_1_out));
  Multiplexer #(.Bits(8)) multiplexer_2 (
    .sel(demultiplexer_1_out_1), .in_0(multiplexer_1_out), .in_1({8{1'b0}}), .out(multiplexer_2_out));
  REGISTER_8 PC (.D(multiplexer_2_out), .E(1'b1), .CLK(and_1_out), .Q(out_4));
  and and_1 (and_1_out, CLK, or_1_out);
  or or_1 (or_1_out, demultiplexer_1_out_0, demultiplexer_1_out_1);
  Multiplexer #(.Bits(8)) multiplexer_3 (.sel(demultiplexer_1_out_2), .in_0(out_4), .in_1(IA), .out(multiplexer_3_out));
  and and_2 (and_2_out, demultiplexer_1_out_2, CLK);
  _256_INSTR_MEM _256_instr_mem_1 (
    .A(multiplexer_3_out), .WD(ID), .WE(demultiplexer_1_out_2), .CLK(and_2_out), .RD(_256_instr_mem_1_rd));
  // CTRL_UNIT ctrl_unit_1: pin names not known; wires that end beside it: _256_instr_mem_1_rd, ctrl_unit_1_p2, ctrl_unit_1_p3, ctrl_unit_1_p4, ctrl_unit_1_p5, ctrl_unit_1_p6, ctrl_unit_1_p7, ctrl_unit_1_p8, ctrl_unit_1_p9, ctrl_unit_1_p10, ctrl_unit_1_p11, ctrl_unit_1_p12
  ADD_8 PC_plus_1 (.Cin(1'b0), .A(out_4), .B(8'h1), .S(PC_plus_1_s));  // open: Cout
  ADD_8 PC_plus_Imm (.Cin(1'b0), .A(ctrl_unit_1_p9), .B(out_4), .S(PC_plus_Imm_s));  // open: Cout
  // _8_REGISTER_BANK _8_register_bank_1: pin names not known; wires that end beside it: ctrl_unit_1_p3, ctrl_unit_1_p4, ctrl_unit_1_p5, _8_register_bank_1_p4, ctrl_unit_1_p6, _8_register_bank_1_p6, out_2, out_3
  and and_3 (_8_register_bank_1_p6, demultiplexer_1_out_0, CLK);
  Multiplexer #(.Bits(8)) multiplexer_4 (
    .sel(ctrl_unit_1_p8), .in_0(out_3), .in_1(ctrl_unit_1_p9), .out(multiplexer_4_out));
  // ALU_8 alu_8_1: pin names not known; wires that end beside it: out_2, multiplexer_4_out, ctrl_unit_1_p7, alu_8_1_p4, alu_8_1_p5, alu_8_1_p6
  // CMPU_CTRL cmpu_ctrl_1: pin names not known; wires that end beside it: ctrl_unit_1_p2, alu_8_1_p5, alu_8_1_p6, cmpu_ctrl_1_p4
  Multiplexer #(.Bits(8)) multiplexer_5 (
    .sel(demultiplexer_1_out_3), .in_0(alu_8_1_p4), .in_1(DA), .out(multiplexer_5_out));
  Multiplexer #(.Bits(8)) multiplexer_6 (.sel(demultiplexer_1_out_3), .in_0(out_3), .in_1(DD), .out(multiplexer_6_out));
  Multiplexer multiplexer_7 (.sel(demultiplexer_1_out_3), .in_0(ctrl_unit_1_p11), .in_1(1'b1), .out(multiplexer_7_out));
  and and_4 (and_4_out, or_2_out, CLK);
  or or_2 (or_2_out, demultiplexer_1_out_0, demultiplexer_1_out_3);
  _256B_MEM_IO _256b_mem_io_1 (
    .A(multiplexer_5_out), .WD(multiplexer_6_out), .WE(multiplexer_7_out), .CLK(and_4_out), .IN(IN),
    .RD(_256b_mem_io_1_rd), .OUT(OUT));
  Multiplexer #(.Selector_Bits(2), .Bits(8)) multiplexer_8 (
    .sel(ctrl_unit_1_p10), .in_0(alu_8_1_p4), .in_1(_256b_mem_io_1_rd), .in_2(PC_plus_1_s),
    .in_3(ctrl_unit_1_p9), .out(_8_register_bank_1_p4));
  Multiplexer #(.Bits(8)) multiplexer_9 (
    .sel(cmpu_ctrl_1_p4), .in_0(PC_plus_1_s), .in_1(PC_plus_Imm_s), .out(multiplexer_9_out));

  // Notes on the sheet:
  //   Modes:
  //   00 - Execution
  //   01 - Reset PC
  //   10 - Program Instruction Memory
  //   11 - Program Data Memory
endmodule
