// Digital circuit CPU.dig as structural Verilog
module CPU (
  input  CLK,
  input  [15:0] IN,
  input  PROGRAM,
  input  [7:0] IA,
  input  [15:0] ID,
  input  [7:0] DA,
  input  [7:0] DD,
  output [47:0] OUT
);

  wire _8_register_bank_1_p6, alu_8_1_p5, alu_8_1_p6, and_1_out, cmpu_ctrl_1_p4, ctrl_unit_1_p2,
       ctrl_unit_1_p3, ctrl_unit_1_p4, ctrl_unit_1_p5, ctrl_unit_1_p6, ctrl_unit_1_p7, ctrl_unit_1_p8,
       ctrl_unit_1_p11, d_flipflop_1_nq, d_flipflop_1_q, multiplexer_7_out;
  wire [1:0] ctrl_unit_1_p10, ctrl_unit_1_p12;
  wire [7:0] _8_register_bank_1_p4, _8_register_bank_1_p7, _8_register_bank_1_p8, _256b_mem_io_1_rd,
       alu_8_1_p4, ctrl_unit_1_p9, multiplexer_1_out, multiplexer_2_out, multiplexer_3_out,
       multiplexer_4_out, multiplexer_5_out, multiplexer_6_out, multiplexer_9_out, PC_plus_1_s,
       PC_plus_Imm_s, PC_q;
  wire [15:0] _256_instr_mem_1_rd;

  D_FLIPFLOP d_flipflop_1 (.D(PROGRAM), .CLK(CLK), .Q(d_flipflop_1_q), .NQ(d_flipflop_1_nq));
  Multiplexer #(.Selector_Bits(2), .Bits(8)) multiplexer_1 (
    .sel(ctrl_unit_1_p12), .in_0(PC_plus_1_s), .in_1(ctrl_unit_1_p9), .in_2(_8_register_bank_1_p7),
    .in_3(multiplexer_9_out), .out(multiplexer_1_out));
  Multiplexer #(.Bits(8)) multiplexer_2 (
    .sel(d_flipflop_1_q), .in_0(multiplexer_1_out), .in_1({8{1'b0}}), .out(multiplexer_2_out));
  REGISTER_8 PC (.D(multiplexer_2_out), .E(1'b1), .CLK(CLK), .Q(PC_q));
  Multiplexer #(.Bits(8)) multiplexer_3 (.sel(d_flipflop_1_q), .in_0(PC_q), .in_1(IA), .out(multiplexer_3_out));
  and and_1 (and_1_out, d_flipflop_1_q, CLK);
  _256_INSTR_MEM _256_instr_mem_1 (
    .A(multiplexer_3_out), .WD(ID), .WE(d_flipflop_1_q), .CLK(and_1_out), .RD(_256_instr_mem_1_rd));
  // CTRL_UNIT ctrl_unit_1: pin names not known; wires that end beside it: _256_instr_mem_1_rd, ctrl_unit_1_p2, ctrl_unit_1_p3, ctrl_unit_1_p4, ctrl_unit_1_p5, ctrl_unit_1_p6, ctrl_unit_1_p7, ctrl_unit_1_p8, ctrl_unit_1_p9, ctrl_unit_1_p10, ctrl_unit_1_p11, ctrl_unit_1_p12
  ADD_8 PC_plus_1 (.Cin(1'b0), .A(PC_q), .B(8'h1), .S(PC_plus_1_s));  // open: Cout
  ADD_8 PC_plus_Imm (.Cin(1'b0), .A(ctrl_unit_1_p9), .B(PC_q), .S(PC_plus_Imm_s));  // open: Cout
  // _8_REGISTER_BANK _8_register_bank_1: pin names not known; wires that end beside it: ctrl_unit_1_p3, ctrl_unit_1_p4, ctrl_unit_1_p5, _8_register_bank_1_p4, ctrl_unit_1_p6, _8_register_bank_1_p6, _8_register_bank_1_p7, _8_register_bank_1_p8
  and and_2 (_8_register_bank_1_p6, d_flipflop_1_nq, CLK);
  Multiplexer #(.Bits(8)) multiplexer_4 (
    .sel(ctrl_unit_1_p8), .in_0(_8_register_bank_1_p8), .in_1(ctrl_unit_1_p9), .out(multiplexer_4_out));
  // ALU_8 alu_8_1: pin names not known; wires that end beside it: _8_register_bank_1_p7, multiplexer_4_out, ctrl_unit_1_p7, alu_8_1_p4, alu_8_1_p5, alu_8_1_p6
  // CMPU_CTRL cmpu_ctrl_1: pin names not known; wires that end beside it: ctrl_unit_1_p2, alu_8_1_p5, alu_8_1_p6, cmpu_ctrl_1_p4
  Multiplexer #(.Bits(8)) multiplexer_5 (.sel(d_flipflop_1_q), .in_0(alu_8_1_p4), .in_1(DA), .out(multiplexer_5_out));
  Multiplexer #(.Bits(8)) multiplexer_6 (
    .sel(d_flipflop_1_q), .in_0(_8_register_bank_1_p8), .in_1(DD), .out(multiplexer_6_out));
  Multiplexer multiplexer_7 (.sel(d_flipflop_1_q), .in_0(ctrl_unit_1_p11), .in_1(1'b1), .out(multiplexer_7_out));
  _256B_MEM_IO _256b_mem_io_1 (
    .A(multiplexer_5_out), .WD(multiplexer_6_out), .WE(multiplexer_7_out), .CLK(CLK), .IN(IN),
    .RD(_256b_mem_io_1_rd), .OUT(OUT));
  Multiplexer #(.Selector_Bits(2), .Bits(8)) multiplexer_8 (
    .sel(ctrl_unit_1_p10), .in_0(alu_8_1_p4), .in_1(_256b_mem_io_1_rd), .in_2(PC_plus_1_s),
    .in_3(ctrl_unit_1_p9), .out(_8_register_bank_1_p4));
  Multiplexer #(.Bits(8)) multiplexer_9 (
    .sel(cmpu_ctrl_1_p4), .in_0(PC_plus_1_s), .in_1(PC_plus_Imm_s), .out(multiplexer_9_out));

  // Notes on the sheet:
  //   Sync signal with clock
  //   Program Mode
  //   Run Mode
endmodule
