// Digital circuit CTRL_UNIT.dig as structural Verilog
module CTRL_UNIT (
  input  [15:0] INSTR,
  output [2:0] RSA1,
  output [2:0] RSA2,
  output [2:0] RDA,
  output RWE,
  output [2:0] ALOP,
  output OP2Sel,
  output [7:0] OP2Im,
  output [1:0] RDSrc,
  output MemWE,
  output [1:0] PCNext
);

  wire and_1_out, and_2_out, and_3_out, and_5_out, and_6_out, and_7_out, and_8_out, nor_1_out, nor_2_out,
       or_1_out;

  and and_1 (and_1_out, ~INSTR[0], INSTR[1]);  // And
  nor nor_1 (nor_1_out, INSTR[0], INSTR[1]);
  nor nor_2 (nor_2_out, INSTR[0], INSTR[1], INSTR[2], INSTR[3]);
  Multiplexer #(.Bits(3)) multiplexer_1 (.sel(and_1_out), .in_0(INSTR[12:10]), .in_1(INSTR[15:13]), .out(RSA1));
  and and_2 (and_2_out, nor_1_out, INSTR[2], ~INSTR[3]);  // And
  and and_3 (and_3_out, nor_1_out, ~INSTR[2], INSTR[3], ~INSTR[4]);  // And
  and and_4 (MemWE, nor_1_out, ~INSTR[2], INSTR[3], INSTR[4]);  // And
  and and_5 (and_5_out, nor_1_out, INSTR[2], INSTR[3]);
  and and_6 (and_6_out, nor_2_out, INSTR[4], ~INSTR[5], ~INSTR[6]);  // And
  and and_7 (and_7_out, nor_2_out, ~INSTR[4], INSTR[5], ~INSTR[6]);  // And
  and and_8 (and_8_out, nor_2_out, INSTR[4], INSTR[5], ~INSTR[6]);  // And
  assign ALOP = and_1_out ? INSTR[4:2] : 3'bz;  // Driver driver_1
  assign RWE = and_2_out ? and_2_out : 1'bz;  // Driver driver_2
  assign ALOP = and_2_out ? INSTR[6:4] : 3'bz;  // Driver driver_3
  assign RWE = and_3_out ? and_3_out : 1'bz;  // Driver driver_4
  assign RDSrc = and_3_out ? 2'b01 : 2'bz;  // Driver driver_5
  assign OP2Sel = MemWE ? MemWE : 1'bz;  // Driver driver_6
  assign RWE = and_5_out ? INSTR[4] : 1'bz;  // Driver driver_7
  assign RWE = and_6_out ? INSTR[7] : 1'bz;  // Driver driver_8
  assign ALOP = and_7_out ? 3'b000 : 3'bz;  // Driver driver_9
  assign OP2Sel = and_1_out ? and_1_out : 1'bz;  // Driver driver_10
  assign RWE = and_1_out ? and_1_out : 1'bz;  // Driver driver_11
  assign OP2Sel = and_3_out ? and_3_out : 1'bz;  // Driver driver_12
  assign RDSrc = and_5_out ? 2'b10 : 2'bz;  // Driver driver_13
  assign RDSrc = and_6_out ? 2'b10 : 2'bz;  // Driver driver_14
  assign RWE = and_7_out ? 1'b1 : 1'bz;  // Driver driver_15
  assign RWE = and_8_out ? 1'b1 : 1'bz;  // Driver driver_16
  assign PCNext = and_5_out ? 2'b01 : 2'bz;  // Driver driver_17
  assign PCNext = and_6_out ? 2'b10 : 2'bz;  // Driver driver_18
  assign OP2Sel = and_7_out ? 1'b1 : 1'bz;  // Driver driver_19
  assign RDSrc = and_8_out ? 2'b11 : 2'bz;  // Driver driver_20
  PullDown #(.Bits(3)) pulldown_1 (.out(ALOP));
  PullDown pulldown_2 (.out(RWE));
  PullDown pulldown_3 (.out(OP2Sel));
  PullDown #(.Bits(2)) pulldown_4 (.out(RDSrc));
  PullDown #(.Bits(2)) pulldown_5 (.out(PCNext));
  or or_1 (or_1_out, and_5_out, and_3_out);
  assign OP2Im = and_1_out ? INSTR[12:5] : 8'bz;  // Driver driver_21
  assign OP2Im = or_1_out ? {3'b000, INSTR[9:5]} : 8'bz;  // Driver driver_22
  assign OP2Im = and_8_out ? INSTR[14:7] : 8'bz;  // Driver driver_23
  PullDown #(.Bits(8)) pulldown_6 (.out(OP2Im));
  assign OP2Im = MemWE ? {3'b000, INSTR[15:13], INSTR[6:5]} : 8'bz;  // Driver driver_24
  assign OP2Im = and_7_out ? {8{1'b0}} : 8'bz;  // Driver driver_25

  assign RDA = INSTR[15:13];
  assign RSA2 = INSTR[9:7];

  // Notes on the sheet:
  //   Decode 
  //   Instr
  //   Decode 
  //   Registers
  //   Branch Instr.
  //   ALU Imm. Instr.
  //   Write Enable (JR vs JALR)
  //   ALU Imm. Instr. OP
  //   ALU Instr OP
  //   Write Enable (J vs JAL)
  //   Register Source /
  //   Destination Addresses
  //   ALU Instr.
  //   Load Instr.
  //   Store Instr.
  //   JAL Instr.
  //   JALR Instr.
  //   MV Instr.
  //   Select RDA 
  //   as RSA2?
  //   Adds immediate 0 to RS1
  //   and sets RD = Result
  //   Operand 2 Immediate
  //   Input
  //   Decode
  //   Immediates
endmodule
